# Fritzing sketch RemoteControlledGreenhouse (saved by Fritzing 0.9.3b)
breadboards: 1

parts:
  U1 = NodeMCU V1.0
  DHT1 = DHT11 Humitidy and Temperature Sensor
  Componente1 = Soil Moisture Sensor
  Water_Level_Sensor1 = Water Level Sensor
  F1 = Fan - Ventilador [package=THT]
  F2 = Fan - Ventilador [package=THT]
  U2 = RELAY [package=OJ]
  U3 = RELAY [package=OJ]
  LED1 = smd LED [color="Red (633nm)" package="1206 [SMD]"]

nets:
  N1: U1.D0, U3.COIL1
  N2: U1.D1, U2.COIL1
  N3: U1.D2, Componente1.VCC
  N4: U1.D3, Water_Level_Sensor1.VCC
  N5: U1.D4, DHT1.DATA
  3V3: U1.3V3, DHT1.VDD
  GND: U1.GND, DHT1.GND, Componente1.GND, Water_Level_Sensor1.GND, F1.GND, F2.GND, U2.COIL2, U3.COIL2, LED1.cathode
  N6: U1.D6, LED1.anode
  N7: U1.A0, Componente1.SIG, Water_Level_Sensor1.SIG
  5V: F1.5V, F2.5V, U3.NO
  N8: U2.MAIN, U3.MAIN

notes:
  VALVE
  DIGITAL LIGHT SENSOR
  GND
  +5V
  +12V
  -12V
  POWER SUPPLY

custom parts:
  NodeMCU V1.0: ESP8266 based NodeMCU
  DHT11 Humitidy and Temperature Sensor: DHT11 Humidity and Temperature Sensor
  Water Level Sensor: A water level sensor. This sensor operates at 3V to 5V. The Sig (signal) pin outputs an analogue signal that is in proportion to the amount of water in contact with the sensor.
  Fan - Ventilador: Ventilador de 2 pines, se encuentra comunmente en computadoras de escritorio
